# Fritzing sketch Perdix (saved by Fritzing 0.8.3b)
breadboards: 1

parts:
  S1 = H-Bridge with L298N
  Parte5 = Arduino Nano (Rev3.0)
  S2 = H-Bridge with L298N
  M3 = DC Motor
  M4 = DC Motor
  M5 = DC Motor
  VCC1 = Battery block 9V
  VCC2 = Battery block 9V

nets:
  N1: S1.12V, VCC1.+
  GND: S1.GND, Parte5.GND, S2.GND, VCC1.-, VCC2.-
  N2: S1.IN1, Parte5.D7
  N3: S1.IN2, Parte5.D6
  N4: S1.IN3, Parte5.D5
  N5: S1.IN4, Parte5.D4
  N6: S1.OUT3-Motor2, M3.pin_2
  N7: S1.OUT4-Motor2, M3.pin_1
  N8: S1.OUT1-Motor1, M4.pin_2
  N9: S1.OUT2-Motor1, M4.pin_1
  N10: Parte5.D8, S2.IN4
  N11: Parte5.D9, S2.IN3
  VIN: Parte5.VIN, Parte5.5V
  N12: S2.12V, VCC2.+
  N13: S2.OUT3-Motor2, M5.pin_2
  N14: S2.OUT4-Motor2, M5.pin_1

custom parts:
  H-Bridge with L298N: h-bridge
